// Logisim project elevator.circ as structural Verilog: 11 circuits, main circuit main
module main (
  input  in_1,
  input  Overload,
  input  Warning,
  input  Motor_overheat,
  input  Door_IR_sensor,
  output UP,
  output STOP,
  output DOWN,
  output Motor_Up,
  output Motor_down,
  output [6:0] buttons,
  output Door_open,
  output Fan,
  output Door_open_2
);

  wire and_1_out, and_2_out, and_5_out, and_7_out, and_8_out, and_9_out, and_11_out, and_12_out, and_13_out,
       and_14_out, Clk_8_hz_out, comparator_1_gt, comparator_1_lt, d_ff_8_q, d_ff_9_q, d_ff_10_q, d_ff_11_q,
       d_ff_12_q, d_ff_13_q, d_ff_14_q, d_ff_15_q, d_ff_16_q, d_ff_17_q, DC_out, decoder_1_out0,
       decoder_1_out1, decoder_1_out2, decoder_1_out3, decoder_1_out4, decoder_1_out5, decoder_1_out6,
       decoder_2_out0, decoder_2_out1, decoder_2_out2, decoder_2_out3, decoder_2_out4, decoder_2_out5,
       decoder_2_out6, DO_out, E_out, F_out, Floor_sensor_out, multiplexer_2_out, nor_1_out, not_1_out,
       not_2_out, not_3_out, not_4_out, not_5_out, or_1_out, or_3_out, or_4_out, or_5_out, or_6_out,
       priority_encoder_1_gs, t_ff_1_q;
  wire [2:0] floor_q, multiplexer_1_out, priority_encoder_1_out;
  wire [3:0] counter_1_q, counter_2_q;
  wire [6:0] _0_out;

  Clock Clk_8_hz (.out(Clk_8_hz_out));
  LED led_1 (.in(buttons[6]));
  LED led_2 (.in(buttons[4]));
  LED led_3 (.in(buttons[2]));
  LED led_4 (.in(buttons[0]));
  LED led_5 (.in(Door_open));
  LED u_Overload (.in(Overload));
  LED u_Warning (.in(or_3_out));
  Button _6 (.out(_0_out[6]));
  Button _4 (.out(_0_out[4]));
  Button _2 (.out(_0_out[2]));
  Button _0 (.out(_0_out[0]));
  Button E (.out(E_out));
  Button DC (.out(DC_out));
  Hex_Digit_Display hex_digit_display_1 (.value({1'b0, floor_q}));  // open: dp
  D_Flip_Flop d_ff_1 (
    .clk(Clk_8_hz_out), .Q(buttons[0]), .preset(_0_out[0]), .reset(decoder_1_out0));  // open: D, Qn, en
  D_Flip_Flop d_ff_2 (
    .clk(Clk_8_hz_out), .Q(buttons[1]), .preset(_0_out[1]), .reset(decoder_1_out1));  // open: D, Qn, en
  D_Flip_Flop d_ff_3 (
    .clk(Clk_8_hz_out), .Q(buttons[2]), .preset(_0_out[2]), .reset(decoder_1_out2));  // open: D, Qn, en
  D_Flip_Flop d_ff_4 (
    .clk(Clk_8_hz_out), .Q(buttons[3]), .preset(_0_out[3]), .reset(decoder_1_out3));  // open: D, Qn, en
  D_Flip_Flop d_ff_5 (
    .clk(Clk_8_hz_out), .Q(buttons[4]), .preset(_0_out[4]), .reset(decoder_1_out4));  // open: D, Qn, en
  D_Flip_Flop d_ff_6 (
    .clk(Clk_8_hz_out), .Q(buttons[5]), .preset(_0_out[5]), .reset(decoder_1_out5));  // open: D, Qn, en
  D_Flip_Flop d_ff_7 (
    .clk(Clk_8_hz_out), .Q(buttons[6]), .preset(_0_out[6]), .reset(decoder_1_out6));  // open: D, Qn, en
  LED led_6 (.in(buttons[5]));
  Button _5 (.out(_0_out[5]));
  Button _3 (.out(_0_out[3]));
  LED led_7 (.in(buttons[3]));
  LED led_8 (.in(buttons[1]));
  Button _1 (.out(_0_out[1]));
  LED led_9 (.in(Fan));
  Button F (.out(F_out));
  LED Emergency (.in(t_ff_1_q));
  Button DO (.out(DO_out));
  DotMatrix #(.matrixrows(6), .dotshape("circle")) dotmatrix_1 (
    .col0({2'b00, UP, DOWN, 2'b00}), .col1({1'b0, UP, 2'b00, DOWN, 1'b0}), .col2({6{1'b1}}),
    .col3({1'b0, UP, 2'b00, DOWN, 1'b0}), .col4({2'b00, UP, DOWN, 2'b00}));
  Decoder #(.select(3), .enable("false")) decoder_1 (
    .out0(decoder_1_out0), .out1(decoder_1_out1), .out2(decoder_1_out2), .out3(decoder_1_out3),
    .out4(decoder_1_out4), .out5(decoder_1_out5), .out6(decoder_1_out6), .sel(floor_q));  // open: out7
  Priority_Encoder #(.disabled(0)) priority_encoder_1 (
    .in0(buttons[0]), .in1(buttons[1]), .in2(buttons[2]), .in3(buttons[3]), .in4(buttons[4]),
    .in5(buttons[5]), .in6(buttons[6]), .in7(1'b0), .out(priority_encoder_1_out), .en_in(1'b1),
    .gs(priority_encoder_1_gs));  // open: en_out
  J_K_Flip_Flop j_k_ff_1 (.J(F_out), .clk(F_out), .K(F_out), .Q(Fan));  // open: Qn, preset, en, reset
  D_Flip_Flop #(.trigger("falling")) d_ff_8 (
    .clk(buttons[6]), .D(1'b1), .Q(d_ff_8_q), .reset(or_1_out));  // open: Qn, preset, en
  D_Flip_Flop #(.trigger("falling")) d_ff_9 (
    .clk(buttons[5]), .D(1'b1), .Q(d_ff_9_q), .reset(or_1_out));  // open: Qn, preset, en
  D_Flip_Flop #(.trigger("falling")) d_ff_10 (
    .clk(buttons[4]), .D(1'b1), .Q(d_ff_10_q), .reset(or_1_out));  // open: Qn, preset, en
  D_Flip_Flop #(.trigger("falling")) d_ff_11 (
    .clk(buttons[3]), .D(1'b1), .Q(d_ff_11_q), .reset(or_1_out));  // open: Qn, preset, en
  D_Flip_Flop #(.trigger("falling")) d_ff_12 (
    .clk(buttons[2]), .D(1'b1), .Q(d_ff_12_q), .reset(or_1_out));  // open: Qn, preset, en
  D_Flip_Flop #(.trigger("falling")) d_ff_13 (
    .clk(buttons[1]), .D(1'b1), .Q(d_ff_13_q), .reset(or_1_out));  // open: Qn, preset, en
  D_Flip_Flop #(.trigger("falling")) d_ff_14 (
    .clk(buttons[0]), .D(1'b1), .Q(d_ff_14_q), .reset(or_1_out));  // open: Qn, preset, en
  Multiplexer #(.width(3), .enable("false")) multiplexer_1 (
    .in0(floor_q), .in1(priority_encoder_1_out), .out(multiplexer_1_out), .sel(priority_encoder_1_gs));
  D_Flip_Flop d_ff_15 (
    .clk(Door_IR_sensor), .D(not_3_out), .Q(d_ff_15_q), .preset(Door_IR_sensor), .reset(and_2_out));  // open: Qn, en
  or or_1 (or_1_out, DC_out, and_2_out);
  or or_2 (Door_open, d_ff_15_q, d_ff_8_q, d_ff_9_q, d_ff_10_q, d_ff_11_q, d_ff_12_q, d_ff_13_q, d_ff_14_q, d_ff_16_q, d_ff_17_q);
  Comparator #(.width(3), .mode("unsigned")) comparator_1 (
    .a(multiplexer_1_out), .b(floor_q), .gt(comparator_1_gt), .eq(STOP), .lt(comparator_1_lt));
  not not_1 (not_1_out, Door_open);
  not not_2 (not_2_out, STOP);
  nor nor_1 (nor_1_out, or_3_out, t_ff_1_q, Overload);
  not not_3 (not_3_out, and_1_out);
  T_Flip_Flop t_ff_1 (.clk(E_out), .T(E_out), .Q(t_ff_1_q));  // open: Qn, preset, reset, en
  and and_1 (and_1_out, priority_encoder_1_gs, not_1_out, not_2_out, nor_1_out);
  or or_3 (or_3_out, Warning, Motor_overheat);
  D_Flip_Flop d_ff_16 (.clk(DO_out), .D(not_3_out), .Q(d_ff_16_q), .reset(or_1_out));  // open: Qn, preset, en
  and and_2 (and_2_out, counter_1_q[0], counter_1_q[1], counter_1_q[2], counter_1_q[3]);
  and and_3 (UP, nor_1_out, comparator_1_gt);
  and and_4 (DOWN, comparator_1_lt, nor_1_out);
  Counter #(.width(4), .max('hf)) counter_1 (
    .load(1'b0), .D(counter_1_q), .count(Door_open), .Q(counter_1_q), .clk(Clk_8_hz_out), .clr(or_4_out));  // open: carry
  or or_4 (or_4_out, and_2_out, Door_IR_sensor, DC_out);
  Counter #(.width(3), .max('h7)) floor (
    .load(DOWN), .D(floor_q), .count(and_1_out), .Q(floor_q), .clk(multiplexer_2_out));  // open: carry, clr
  Multiplexer #(.enable("false")) multiplexer_2 (
    .in0(and_7_out), .in1(Floor_sensor_out), .out(multiplexer_2_out), .sel(in_1));
  and and_5 (and_5_out, decoder_2_out0, _0_out[0]);
  not not_4 (not_4_out, DOWN);
  and and_6 (Motor_down, DOWN, and_1_out);
  and and_7 (and_7_out, counter_2_q[0], counter_2_q[1], not_5_out, counter_2_q[3]);
  not not_5 (not_5_out, counter_2_q[2]);
  or or_5 (or_5_out, DC_out, or_4_out);
  and and_8 (and_8_out, decoder_2_out2, _0_out[2]);
  and and_9 (and_9_out, decoder_2_out1, _0_out[1]);
  Counter #(.width(4), .max('hb)) counter_2 (
    .load(1'b0), .D(counter_2_q), .count(and_1_out), .Q(counter_2_q), .clk(Clk_8_hz_out),
    .clr(multiplexer_2_out));  // open: carry
  and and_10 (Motor_Up, and_1_out, not_4_out);
  or or_6 (or_6_out, and_5_out, and_9_out, and_8_out, and_11_out, and_12_out, and_13_out, and_14_out);
  and and_11 (and_11_out, decoder_2_out3, _0_out[3]);
  and and_12 (and_12_out, decoder_2_out4, _0_out[4]);
  D_Flip_Flop d_ff_17 (.clk(or_6_out), .D(not_3_out), .Q(d_ff_17_q), .reset(or_5_out));  // open: Qn, preset, en
  and and_13 (and_13_out, decoder_2_out5, _0_out[5]);
  and and_14 (and_14_out, decoder_2_out6, _0_out[6]);
  Button Floor_sensor (.out(Floor_sensor_out));
  Decoder #(.select(3), .enable("false")) decoder_2 (
    .out0(decoder_2_out0), .out1(decoder_2_out1), .out2(decoder_2_out2), .out3(decoder_2_out3),
    .out4(decoder_2_out4), .out5(decoder_2_out5), .out6(decoder_2_out6), .sel(floor_q));  // open: out7

  assign Door_open_2 = Door_open;

  // Notes on the sheet:
  //   Door close
  //   Fan
  //   Door open
  //   0 for automated counter, 1 for using the floor sensor
endmodule

// 74191
module _74191_counter (
  input  Vcc,
  input  P1,
  input  P0,
  input  Clk,
  input  RC_prime,
  input  TC,
  input  PL_prime,
  input  P2,
  input  CE_prime___Coount,
  input  P3,
  input  U_prime_D___load,
  input  Gnd,
  output Q1,
  output Q0,
  output Q2,
  output Q3
);

  wire not_1_out, undriven;

  not not_1 (not_1_out, CE_prime___Coount);
  Counter #(.width(4), .max('hf)) counter_1 (
    .load(U_prime_D___load), .D({P3, P2, P1, P0}), .count(not_1_out), .Q({Q3, Q2, Q1, Q0}), .clk(Clk),
    .clr(undriven));  // open: carry
endmodule

// 74157
module _74157_2x1_mux_4 (
  input  _1__S,
  input  _16__Vcc,
  input  _2__A1,
  input  _15__G,
  input  _3__B1,
  input  _14__A4,
  input  _13__B4,
  input  _5__A2,
  input  _6__B2,
  input  _11__A3,
  input  _10__B3,
  input  _8__GND,
  output _4__Y1,
  output _12__Y4,
  output _7__Y2,
  output _9__Y3
);

  wire multiplexer_1_out, multiplexer_2_out, multiplexer_3_out, multiplexer_4_out, not_1_out;

  Multiplexer #(.enable("false")) multiplexer_1 (.in0(_2__A1), .in1(_3__B1), .out(multiplexer_1_out), .sel(_1__S));
  and and_1 (_4__Y1, multiplexer_1_out, not_1_out);
  Multiplexer #(.enable("false")) multiplexer_2 (.in0(_5__A2), .in1(_6__B2), .out(multiplexer_2_out), .sel(_1__S));
  and and_2 (_7__Y2, multiplexer_2_out, not_1_out);
  not not_1 (not_1_out, _15__G);
  Multiplexer #(.enable("false")) multiplexer_3 (.in0(_14__A4), .in1(_13__B4), .out(multiplexer_3_out), .sel(_1__S));
  and and_3 (_12__Y4, multiplexer_3_out, not_1_out);
  Multiplexer #(.enable("false")) multiplexer_4 (.in0(_11__A3), .in1(_10__B3), .out(multiplexer_4_out), .sel(_1__S));
  and and_4 (_9__Y3, multiplexer_4_out, not_1_out);

  // Notes on the sheet:
  //   74157: Quad 2-Line to 1-Line Multiplexer
endmodule

// 74148
module _74148_pri_enc (
  input  _1__I4,
  input  _16__Vcc,
  input  _2__I5,
  input  _15__nEO__NC,
  input  _3__I6,
  input  _14__nGS__NC,
  input  _4__I7,
  input  _13__I3,
  input  _5__nEI__NC,
  input  _12__I2,
  input  _11__I1,
  input  _10__I0,
  input  _8__GND,
  output _6__A2,
  output _7__A1,
  output _9__A0
);

  Priority_Encoder #(.disabled(0)) priority_encoder_1 (
    .in0(_10__I0), .in1(_11__I1), .in2(_12__I2), .in3(_13__I3), .in4(_1__I4), .in5(_2__I5), .in6(_3__I6),
    .in7(_4__I7), .out({_6__A2, _7__A1, _9__A0}), .en_in(1'b1));  // open: gs, en_out

  // Notes on the sheet:
  //   74148: 9-Line to 4-Line Priority Encoder
  //   NOTE: Pins 5, 14, and 15 have connections normally, but I chose not to model them
endmodule

// 74138
module _74138_3_to_8_decoder (
  input  _1__A,
  input  _16__Vcc,
  input  _2__B,
  input  _3__C,
  input  _4__G2A,
  input  _5__G2B,
  input  _6__G1,
  input  _8__GND,
  output _15__Y0,
  output _14__Y1,
  output _13__Y2,
  output _12__Y3,
  output _11__Y4,
  output _7__Y7,
  output _10__Y5,
  output _9__Y6
);

  wire and_1_out, and_2_out, and_3_out, and_4_out, and_5_out, and_6_out, and_7_out, and_8_out, and_9_out,
       decoder_1_out0, decoder_1_out1, decoder_1_out2, decoder_1_out3, decoder_1_out4, decoder_1_out5,
       decoder_1_out6, decoder_1_out7, not_1_out, not_2_out;

  not not_1 (not_1_out, _4__G2A);
  not not_2 (not_2_out, _5__G2B);
  not not_3 (_7__Y7, and_1_out);
  and and_1 (and_1_out, and_2_out, decoder_1_out7);
  and and_2 (and_2_out, not_1_out, not_2_out, _6__G1);
  Decoder #(.select(3), .enable("false")) decoder_1 (
    .out0(decoder_1_out0), .out1(decoder_1_out1), .out2(decoder_1_out2), .out3(decoder_1_out3),
    .out4(decoder_1_out4), .out5(decoder_1_out5), .out6(decoder_1_out6), .out7(decoder_1_out7),
    .sel({_3__C, _2__B, _1__A}));
  not not_4 (_15__Y0, and_3_out);
  and and_3 (and_3_out, and_2_out, decoder_1_out0);
  and and_4 (and_4_out, and_2_out, decoder_1_out1);
  not not_5 (_14__Y1, and_4_out);
  and and_5 (and_5_out, and_2_out, decoder_1_out2);
  not not_6 (_13__Y2, and_5_out);
  not not_7 (_12__Y3, and_6_out);
  and and_6 (and_6_out, and_2_out, decoder_1_out3);
  not not_8 (_11__Y4, and_7_out);
  and and_7 (and_7_out, and_2_out, decoder_1_out4);
  not not_9 (_10__Y5, and_8_out);
  and and_8 (and_8_out, and_2_out, decoder_1_out5);
  and and_9 (and_9_out, and_2_out, decoder_1_out6);
  not not_10 (_9__Y6, and_9_out);

  // Notes on the sheet:
  //   74138: 3-Line to 8-Line Decoder
endmodule

// 7474
module _7474_D_ff (
  input  _1__CLR1,
  input  _14__Vcc,
  input  _2__D1,
  input  _13__CLR2,
  input  _3__CLK1,
  input  _12__D2,
  input  _4__PR1,
  input  _11__CLK2,
  input  _10__PR2,
  input  _7__GND,
  output _5__Q1,
  output _6__nQ1,
  output _9__Q2,
  output _8__nQ2
);

  D_Flip_Flop d_ff_1 (
    .clk(_3__CLK1), .D(_2__D1), .Q(_5__Q1), .Qn(_6__nQ1), .preset(_4__PR1), .reset(_1__CLR1));  // open: en
  D_Flip_Flop d_ff_2 (
    .clk(_11__CLK2), .D(_12__D2), .Q(_9__Q2), .Qn(_8__nQ2), .preset(_10__PR2), .reset(_13__CLR2));  // open: en

  // Notes on the sheet:
  //   7474: dual D-type flip flop
endmodule

// 7448
module _7448_BCD_7segment (
  input  _1__B,
  input  _16__Vcc,
  input  _2__C,
  input  _3__nLT,
  input  _4__NC,
  input  _5__nRBI,
  input  _6__D,
  input  _7__A,
  input  _8__GND,
  output _15__f,
  output _14__g,
  output _13__a,
  output _12__b,
  output _11__c,
  output _10__d,
  output _9__e
);

  wire and_1_out, and_2_out, nand_1_out, nand_2_out, nand_3_out, nand_4_out, nand_5_out, nand_6_out,
       nand_7_out, nand_8_out, nand_9_out, nand_10_out, nand_11_out, nand_12_out, nand_13_out, nand_14_out,
       nand_15_out, nand_16_out, nand_17_out, nand_18_out, nand_19_out, nand_20_out, nand_21_out,
       nand_22_out, nand_23_out, nand_24_out, nand_25_out, not_1_out, not_2_out, not_3_out;

  nand nand_1 (nand_1_out, _7__A, _3__nLT);
  nand nand_2 (nand_2_out, _1__B, _3__nLT);
  nand nand_3 (nand_3_out, _2__C, _3__nLT);
  not not_1 (not_1_out, _6__D);
  not not_2 (not_2_out, _5__nRBI);
  and and_1 (and_1_out, _1__B, _2__C, ~_6__D, ~_7__A);  // AND_Gate
  nand nand_4 (nand_4_out, nand_1_out, nand_8_out);
  nand nand_5 (nand_5_out, nand_2_out, nand_8_out);
  nand nand_6 (nand_6_out, nand_3_out, nand_8_out);
  nand nand_7 (nand_7_out, not_1_out, nand_8_out);
  nand nand_8 (nand_8_out, _3__nLT, _3__nLT, not_2_out, not_1_out, nand_3_out, nand_2_out, nand_1_out);
  nand nand_9 (nand_9_out, nand_5_out, nand_7_out);
  nand nand_10 (nand_10_out, nand_1_out, nand_6_out);
  nand nand_11 (nand_11_out, nand_4_out, nand_4_out, nand_2_out, nand_3_out, not_1_out);
  nand nand_12 (nand_12_out, nand_5_out, nand_7_out);
  nand nand_13 (nand_13_out, nand_4_out, nand_2_out, nand_6_out);
  nand nand_14 (nand_14_out, nand_1_out, nand_5_out, nand_6_out);
  nand nand_15 (nand_15_out, nand_6_out, nand_7_out);
  nand nand_16 (nand_16_out, nand_1_out, nand_5_out, nand_3_out);
  nand nand_17 (nand_17_out, nand_4_out, nand_2_out, nand_3_out);
  nand nand_18 (nand_18_out, nand_1_out, nand_2_out, nand_6_out);
  nand nand_19 (nand_19_out, nand_4_out, nand_5_out, nand_6_out);
  not not_3 (not_3_out, nand_4_out);
  nand nand_20 (nand_20_out, nand_2_out, nand_6_out);
  nand nand_21 (nand_21_out, nand_4_out, nand_5_out);
  nand nand_22 (nand_22_out, nand_5_out, nand_3_out);
  nand nand_23 (nand_23_out, nand_4_out, nand_3_out, not_1_out);
  nand nand_24 (nand_24_out, nand_4_out, nand_5_out, nand_6_out);
  nand nand_25 (nand_25_out, nand_2_out, nand_3_out, not_1_out, _3__nLT);
  and and_2 (and_2_out, nand_9_out, nand_10_out, nand_11_out);
  and and_3 (_12__b, nand_12_out, nand_13_out, nand_14_out);
  and and_4 (_11__c, nand_15_out, nand_16_out);
  and and_5 (_10__d, nand_17_out, nand_18_out, nand_19_out);
  and and_6 (_9__e, not_3_out, nand_20_out);
  and and_7 (_15__f, nand_21_out, nand_22_out, nand_23_out);
  and and_8 (_14__g, nand_24_out, nand_25_out);
  or or_1 (_13__a, and_2_out, and_1_out);

  // Notes on the sheet:
  //   7448: BCD to 7-segment decoder
endmodule

module IC_new (
  output Motor_up,
  output out_2,
  output out_3,
  output out_4,
  output Motor_down
);

  wire _0_out, _1_out, _2_out, _3_out, _4_out, _5_out, _6_out, clock_1_out, Floor_sensor_out,
       n7404_inverter_1__12__6y, n7404_inverter_2__2__1y, n7404_inverter_2__4__2y, n7404_inverter_2__6__3y,
       n7404_inverter_2__8__4y, n7404_inverter_2__10__5y, n7404_inverter_2__12__6y, n7432_or_1__3__1y,
       n7432_or_1__6__2y, n7432_or_1__8__3y, n7432_or_1__11__4y, n7432_or_2__3__1y, n7432_or_2__6__2y,
       n7474_d_ff_1__5__q1, n7474_d_ff_1__9__q2, n7474_d_ff_2__5__q1, n7474_d_ff_2__9__q2,
       n7474_d_ff_3__5__q1, n7474_d_ff_3__9__q2, n7474_d_ff_4__5__q1, n74138_3_to_8_decoder_1__9__y6,
       n74138_3_to_8_decoder_1__10__y5, n74138_3_to_8_decoder_1__11__y4, n74138_3_to_8_decoder_1__12__y3,
       n74138_3_to_8_decoder_1__13__y2, n74138_3_to_8_decoder_1__14__y1, n74138_3_to_8_decoder_1__15__y0,
       n74148_pri_enc_1__6__a2, n74148_pri_enc_1__7__a1, n74148_pri_enc_1__9__a0, n74157_2x1_mux_4_1__4__y1,
       n74157_2x1_mux_4_1__7__y2, n74157_2x1_mux_4_1__9__y3, n74157_2x1_mux_4_1__12__y4;
  wire [3:0] n74191_counter_1_q0;
  wire [6:0] n7448_bcd_7segment_1__15__f;

  LED led_1 (.in(n7474_d_ff_1__5__q1));
  LED led_2 (.in(n7474_d_ff_1__9__q2));
  LED led_3 (.in(n7474_d_ff_2__5__q1));
  LED led_4 (.in(n7474_d_ff_2__9__q2));
  LED led_5 (.in(n7474_d_ff_3__5__q1));
  LED led_6 (.in(n7474_d_ff_3__9__q2));
  LED led_7 (.in(n7474_d_ff_4__5__q1));
  Clock clock_1 (.out(clock_1_out));
  Button _0 (.out(_0_out));
  Button _1 (.out(_1_out));
  Button _2 (.out(_2_out));
  Button _3 (.out(_3_out));
  Button _4 (.out(_4_out));
  Button _5 (.out(_5_out));
  Button _6 (.out(_6_out));
  LED Up (.in(Motor_up));
  LED Down (.in(Motor_down));
  _7_Segment_Display u_7_segment_display_1 (
    .g(n7448_bcd_7segment_1__15__f[1]), .f(n7448_bcd_7segment_1__15__f[0]),
    .a(n7448_bcd_7segment_1__15__f[5]), .b(n7448_bcd_7segment_1__15__f[3]),
    .e(n7448_bcd_7segment_1__15__f[6]), .d(n7448_bcd_7segment_1__15__f[2]), .c(n7448_bcd_7segment_1__15__f[4]));  // open: dp
  _7474_D_ff u_7474_d_ff_1 (
    ._1__CLR1(n7404_inverter_2__2__1y), ._3__CLK1(clock_1_out), ._4__PR1(_0_out),
    ._5__Q1(n7474_d_ff_1__5__q1), ._7__GND(n74191_counter_1_q0[3]), ._14__Vcc(1'b1),
    ._13__CLR2(n7404_inverter_2__4__2y), ._11__CLK2(clock_1_out), ._10__PR2(_1_out),
    ._9__Q2(n7474_d_ff_1__9__q2));  // open: _2__D1, _6__nQ1, _12__D2, _8__nQ2
  _7474_D_ff u_7474_d_ff_2 (
    ._1__CLR1(n7404_inverter_2__6__3y), ._3__CLK1(clock_1_out), ._4__PR1(_2_out),
    ._5__Q1(n7474_d_ff_2__5__q1), ._7__GND(n74191_counter_1_q0[3]), ._14__Vcc(1'b1),
    ._13__CLR2(n7404_inverter_2__12__6y), ._11__CLK2(clock_1_out), ._10__PR2(_3_out),
    ._9__Q2(n7474_d_ff_2__9__q2));  // open: _2__D1, _6__nQ1, _12__D2, _8__nQ2
  _7474_D_ff u_7474_d_ff_3 (
    ._1__CLR1(n7404_inverter_2__10__5y), ._3__CLK1(clock_1_out), ._4__PR1(_4_out),
    ._5__Q1(n7474_d_ff_3__5__q1), ._7__GND(n74191_counter_1_q0[3]), ._14__Vcc(1'b1),
    ._13__CLR2(n7404_inverter_2__8__4y), ._11__CLK2(clock_1_out), ._10__PR2(_5_out),
    ._9__Q2(n7474_d_ff_3__9__q2));  // open: _2__D1, _6__nQ1, _12__D2, _8__nQ2
  _7474_D_ff u_7474_d_ff_4 (
    ._1__CLR1(n7404_inverter_1__12__6y), ._3__CLK1(clock_1_out), ._4__PR1(_6_out),
    ._5__Q1(n7474_d_ff_4__5__q1), ._7__GND(n74191_counter_1_q0[3]), ._14__Vcc(1'b1));  // open: _2__D1, _6__nQ1, _13__CLR2, _12__D2, _11__CLK2, _10__PR2, _9__Q2, _8__nQ2
  _7404_inverter u_7404_inverter_1 (
    ._7__GND(n74191_counter_1_q0[3]), ._14__Vcc(1'b1), ._13__6A(n74138_3_to_8_decoder_1__9__y6),
    ._12__6Y(n7404_inverter_1__12__6y));  // open: _1__1A, _2__1Y, _3__2A, _4__2Y, _5__3A, _6__3Y, _11__5A, _10__5Y, _9__4A, _8__4Y
  _74138_3_to_8_decoder u_74138_3_to_8_decoder_1 (
    ._1__A(n74191_counter_1_q0[0]), ._2__B(n74191_counter_1_q0[1]), ._3__C(n74191_counter_1_q0[2]),
    ._4__G2A(n74191_counter_1_q0[3]), ._5__G2B(n74191_counter_1_q0[3]), ._6__G1(1'b1),
    ._8__GND(n74191_counter_1_q0[3]), ._16__Vcc(1'b1), ._15__Y0(n74138_3_to_8_decoder_1__15__y0),
    ._14__Y1(n74138_3_to_8_decoder_1__14__y1), ._13__Y2(n74138_3_to_8_decoder_1__13__y2),
    ._12__Y3(n74138_3_to_8_decoder_1__12__y3), ._11__Y4(n74138_3_to_8_decoder_1__11__y4),
    ._10__Y5(n74138_3_to_8_decoder_1__10__y5), ._9__Y6(n74138_3_to_8_decoder_1__9__y6));  // open: _7__Y7
  _7404_inverter u_7404_inverter_2 (
    ._1__1A(n74138_3_to_8_decoder_1__15__y0), ._2__1Y(n7404_inverter_2__2__1y),
    ._3__2A(n74138_3_to_8_decoder_1__14__y1), ._4__2Y(n7404_inverter_2__4__2y),
    ._5__3A(n74138_3_to_8_decoder_1__13__y2), ._6__3Y(n7404_inverter_2__6__3y),
    ._7__GND(n74191_counter_1_q0[3]), ._14__Vcc(1'b1), ._13__6A(n74138_3_to_8_decoder_1__12__y3),
    ._12__6Y(n7404_inverter_2__12__6y), ._11__5A(n74138_3_to_8_decoder_1__11__y4),
    ._10__5Y(n7404_inverter_2__10__5y), ._9__4A(n74138_3_to_8_decoder_1__10__y5),
    ._8__4Y(n7404_inverter_2__8__4y));
  _74148_pri_enc u_74148_pri_enc_1 (
    ._1__I4(n7474_d_ff_3__5__q1), ._2__I5(n7474_d_ff_3__9__q2), ._3__I6(n7474_d_ff_4__5__q1),
    ._4__I7(n74191_counter_1_q0[3]), ._6__A2(n74148_pri_enc_1__6__a2), ._7__A1(n74148_pri_enc_1__7__a1),
    ._8__GND(n74191_counter_1_q0[3]), ._16__Vcc(1'b1), ._13__I3(n7474_d_ff_2__9__q2),
    ._12__I2(n7474_d_ff_2__5__q1), ._11__I1(n7474_d_ff_1__9__q2), ._10__I0(n7474_d_ff_1__5__q1),
    ._9__A0(n74148_pri_enc_1__9__a0));  // open: _5__nEI__NC, _15__nEO__NC, _14__nGS__NC
  _7432_or u_7432_or_1 (
    ._1__1A(n7474_d_ff_3__5__q1), ._2__1B(n7474_d_ff_3__9__q2), ._3__1Y(n7432_or_1__3__1y),
    ._4__2A(n7432_or_1__3__1y), ._5__2B(n7474_d_ff_4__5__q1), ._6__2Y(n7432_or_1__6__2y),
    ._7__GND(n74191_counter_1_q0[3]), ._14__Vcc(1'b1), ._13__4B(n7474_d_ff_1__5__q1),
    ._12__4A(n7474_d_ff_1__9__q2), ._11__4Y(n7432_or_1__11__4y), ._10__3B(n7432_or_1__11__4y),
    ._9__3A(n7474_d_ff_2__5__q1), ._8__3Y(n7432_or_1__8__3y));
  _7432_or u_7432_or_2 (
    ._1__1A(n7432_or_1__8__3y), ._2__1B(n7432_or_1__6__2y), ._3__1Y(n7432_or_2__3__1y),
    ._4__2A(n7432_or_2__3__1y), ._5__2B(n7474_d_ff_2__9__q2), ._6__2Y(n7432_or_2__6__2y),
    ._7__GND(n74191_counter_1_q0[3]), ._14__Vcc(1'b1));  // open: _13__4B, _12__4A, _11__4Y, _10__3B, _9__3A, _8__3Y
  _7448_BCD_7segment u_7448_bcd_7segment_1 (
    ._1__B(n74191_counter_1_q0[1]), ._2__C(n74191_counter_1_q0[2]), ._3__nLT(1'b1), ._5__nRBI(1'b1),
    ._6__D(n74191_counter_1_q0[3]), ._7__A(n74191_counter_1_q0[0]), ._8__GND(n74191_counter_1_q0[3]),
    ._16__Vcc(1'b1), ._15__f(n7448_bcd_7segment_1__15__f[0]), ._14__g(n7448_bcd_7segment_1__15__f[1]),
    ._13__a(n7448_bcd_7segment_1__15__f[2]), ._12__b(n7448_bcd_7segment_1__15__f[3]),
    ._11__c(n7448_bcd_7segment_1__15__f[4]), ._10__d(n7448_bcd_7segment_1__15__f[5]),
    ._9__e(n7448_bcd_7segment_1__15__f[6]));  // open: _4__NC
  _74157_2x1_mux_4 u_74157_2x1_mux_4_1 (
    ._1__S(n7432_or_2__6__2y), ._2__A1(n74191_counter_1_q0[0]), ._3__B1(n74148_pri_enc_1__9__a0),
    ._4__Y1(n74157_2x1_mux_4_1__4__y1), ._5__A2(n74191_counter_1_q0[1]), ._6__B2(n74148_pri_enc_1__7__a1),
    ._7__Y2(n74157_2x1_mux_4_1__7__y2), ._8__GND(n74191_counter_1_q0[3]), ._16__Vcc(1'b1),
    ._15__G(n74191_counter_1_q0[3]), ._14__A4(n74191_counter_1_q0[3]), ._13__B4(n74191_counter_1_q0[3]),
    ._12__Y4(n74157_2x1_mux_4_1__12__y4), ._11__A3(n74191_counter_1_q0[2]),
    ._10__B3(n74148_pri_enc_1__6__a2), ._9__Y3(n74157_2x1_mux_4_1__9__y3));
  _7485_comparator u_7485_comparator_1 (
    .B3(n74191_counter_1_q0[3]), .A_Bout(Motor_up), .A_Bout_2(out_3), .A_Bout_3(Motor_down),
    .Gnd(n74191_counter_1_q0[3]), .Vcc(1'b1), .A0(n74157_2x1_mux_4_1__4__y1), .A1(n74157_2x1_mux_4_1__7__y2),
    .A2(n74157_2x1_mux_4_1__9__y3), .A3(n74157_2x1_mux_4_1__12__y4), .B0(n74191_counter_1_q0[0]),
    .B1(n74191_counter_1_q0[1]), .B2(n74191_counter_1_q0[2]));  // open: A_Bin, A_Bin_2, A_Bin_3
  _74191_counter u_74191_counter_1 (
    .Vcc(1'b1), .P1(n74191_counter_1_q0[1]), .CE_prime___Coount(out_3), .U_prime_D___load(Motor_down),
    .Gnd(n74191_counter_1_q0[3]), .P0(n74191_counter_1_q0[0]), .Clk(Floor_sensor_out),
    .P2(n74191_counter_1_q0[2]), .P3(n74191_counter_1_q0[3]), .Q1(n74191_counter_1_q0[1]),
    .Q0(n74191_counter_1_q0[0]), .Q2(n74191_counter_1_q0[2]), .Q3(n74191_counter_1_q0[3]));  // open: RC_prime, TC, PL_prime
  Button Floor_sensor (.out(Floor_sensor_out));

  assign out_2 = Motor_up;
  assign out_4 = Motor_down;
  // also tied to GND on the sheet: n74191_counter_1_q0[3]
endmodule

// 7485
module _7485_comparator (
  input  Vcc,
  input  B3,
  input  A0,
  input  A1,
  input  A2,
  input  A_Bin,
  input  A3,
  input  A_Bin_2,
  input  A_Bin_3,
  input  B0,
  input  B1,
  input  B2,
  input  Gnd,
  output A_Bout,
  output A_Bout_2,
  output A_Bout_3
);

  Comparator #(.width(4), .mode("unsigned")) comparator_1 (
    .a({A3, A2, A1, A0}), .b({B3, B2, B1, B0}), .gt(A_Bout), .eq(A_Bout_2), .lt(A_Bout_3));
endmodule

// 7404
module _7404_inverter (
  input  _1__1A,
  input  _14__Vcc,
  input  _13__6A,
  input  _3__2A,
  input  _11__5A,
  input  _5__3A,
  input  _9__4A,
  input  _7__GND,
  output _2__1Y,
  output _12__6Y,
  output _4__2Y,
  output _10__5Y,
  output _6__3Y,
  output _8__4Y
);

  not not_1 (_2__1Y, _1__1A);
  not not_2 (_4__2Y, _3__2A);
  not not_3 (_6__3Y, _5__3A);
  not not_4 (_12__6Y, _13__6A);
  not not_5 (_10__5Y, _11__5A);
  not not_6 (_8__4Y, _9__4A);

  // Notes on the sheet:
  //   7407: hex inverter
endmodule

// 7432
module _7432_or (
  input  _1__1A,
  input  _14__Vcc,
  input  _2__1B,
  input  _13__4B,
  input  _12__4A,
  input  _4__2A,
  input  _5__2B,
  input  _10__3B,
  input  _9__3A,
  input  _7__GND,
  output _3__1Y,
  output _11__4Y,
  output _6__2Y,
  output _8__3Y
);

  or or_1 (_3__1Y, _2__1B, _1__1A);
  or or_2 (_6__2Y, _5__2B, _4__2A);
  or or_3 (_11__4Y, _13__4B, _12__4A);
  or or_4 (_8__3Y, _10__3B, _9__3A);

  // Notes on the sheet:
  //   7432: quad OR
endmodule
